# Fritzing sketch circuit (saved by Fritzing 0.9.3b)
breadboards: 2

parts:
  Part1 = Arduino Uno (Rev3)
  Part2 = Thumb Joystick
  S1 = Pushbutton [package="[SMD]"]
  R1 = Trimmer Potentiometer [maximum_resistance=10kΩ package=THT]
  J1 = Piezo Speaker
  Disp1 = LBT2088AH [part_number=LBT2088AH]
  U1 = LCD-16X2 [package=lcd-16x2_noholes]
  R2 = Resistor [tolerance=±5% resistance=10 package="0603 [SMD]"]
  R3 = Resistor [tolerance=±5% resistance=10k package="2512 [SMD]"]
  U2 = MAX7219 [package=dil24]
  C1 = Electrolytic Capacitor [capacitance=10μF package="0605 [SMD, electrolytic]"]
  C2 = Ceramic Capacitor [capacitance=100nF package="100 mil [THT, multilayer]"]
  R4 = Resistor [tolerance=±5% resistance=220 package="2512 [SMD]"]
  R5 = Resistor [tolerance=±5% resistance=100k package="0603 [SMD]"]

nets:
  N1: Part1.A0, Part2.VERT
  N2: Part1.A1, Part2.HORZ
  N3: Part1.A5/SCL, R2.Pin_1
  N4: Part1.D8, U1.E
  N5: Part1.D9_PWM, U1.RS
  N6: Part1.D10_PWM/SS, U2.LOAD
  N7: Part1.D11_PWM/MOSI, U2.CLK
  N8: Part1.D12/MISO, U2.DIN
  N9: Part1.D2, Part2.SEL
  N10: Part1.D3_PWM, S1.Pin_1, S1.Pin_2, R3.Pin_0
  N11: Part1.D4, U1.DB7
  N12: Part1.D5_PWM, U1.DB6
  N13: Part1.D6_PWM, U1.DB5
  N14: Part1.D7, U1.DB4
  VCC: Part1.5V, Part2.VCC, S1.Pin_3, S1.Pin_4, R1.leg1, U1.VDD, U2.VCC, C1.+, C2.1, R4.Pin_0, R5.Pin_0
  GND: Part1.GND, Part2.GND, R1.leg2, J1.pin1, U1.VSS, U1.R_W, U1.K, R3.Pin_1, U2.GND, U2.GND2, C1.-, C2.0
  N15: R1.wiper, U1.VO
  N16: J1.pin2, R2.Pin_0
  N17: Disp1.pin1, U2.DIG4
  N18: Disp1.pin2, U2.DIG6
  N19: Disp1.pin_3, U2.SEGA
  N20: Disp1.pin_4, U2.SEGB
  N21: Disp1.pin_5, U2.DIG7
  N22: Disp1.pin_6, U2.SEGD
  N23: Disp1.pin_7, U2.DIG5
  N24: Disp1.pin_8, U2.DIG2
  N25: Disp1.pin_9, U2.DIG0
  N26: Disp1.pin_10, U2.SEGC
  N27: Disp1.pin_11, U2.SEGE
  N28: Disp1.pin_12, U2.DIG3
  N29: Disp1.pin_13, U2.SEGDP
  N30: Disp1.pin_14, U2.DIG1
  N31: Disp1.pin_15, U2.SEGF
  N32: Disp1.pin_16, U2.SEGG
  N33: U1.A, R4.Pin_1
  N34: U2.ISET, R5.Pin_1

notes:
  220Ω
  100kΩ
  10Ω
  10μF
  10kΩ
  100nF
